# Fritzing sketch Temperatursensor (saved by Fritzing 0.9.3b)
circuit board: 5.61309cm x 3.89928cm
perfboards: 1

parts:
  DHT22 = Humidity and Temperature Sensor RHT03
  ESP12E = ESP8266 WiFi Module [part_number=ESP8266]
  R1 = Resistor [tolerance=±5% resistance=10k package=THT]
  C2 = Ceramic Capacitor [capacitance=1µF package="0603 [SMD, multilayer]"]
  C1 = Ceramic Capacitor [capacitance=1µF package="0603 [SMD, multilayer]"]
  USB-to-UART = FTDI Basic Programmer
  VREG = Voltage Regulator [package=to220-adj]
  R2 = Resistor [tolerance=±5% resistance=470 package=THT]
  R3 = Resistor [tolerance=±5% resistance=470k package=THT]
  V_BATT = Battery
  R4 = Resistor [tolerance=±5% resistance=220k package=THT]
  R5 = Resistor [tolerance=±5% resistance=100k package=THT]
  JP_BATT = Header 2 [package=molex-1x2_lock]
  JP_VCC = Header 2 [package=molex-1x2_lock]
  JP_RST = Header 2 [package=molex-1x2_lock]
  JP_PRG = Header 2 [package=molex-1x2_lock]
  JP_SERIAL = Header 2 [package=molex-1x2_lock]

nets:
  VCC: DHT22.Vcc, ESP12E.VCC, R1.Pin_0, C2.1, USB-to-UART.POWER, VREG.OUT, JP_VCC.1
  N1: DHT22.Data-signal, ESP12E.GPIO_0, R1.Pin_1
  GND: DHT22.GND_2, ESP12E.GND, C2.0, USB-to-UART.GND, R5.Pin_0, JP_RST.1, JP_PRG.2
  N2: ESP12E.RXD, USB-to-UART.TXO, JP_SERIAL.2
  N3: ESP12E.TXD, USB-to-UART.RXI, JP_SERIAL.1
  N4: ESP12E.GPIO_4, JP_PRG.1
  N5: ESP12E.ADC_0, R4.Pin_1, R5.Pin_1
  N6: ESP12E.GPIO_16, R2.Pin_0
  N7: ESP12E.REST, R2.Pin_1, JP_RST.2
  N8: C1.0, VREG.IN, R3.Pin_0, V_BATT.+, JP_BATT.1
  N9: C1.1, VREG.ADJ, V_BATT.-, JP_BATT.2, JP_VCC.2
  N10: R3.Pin_1, R4.Pin_0
